# Fritzing sketch Module 4 Fritzing Sketch (saved by Fritzing 0.9.3b)

parts:
  Componente3 = Arduino Nano (Rev3.0)
  ZS-042_RTC1 = ZS-042 RTC Module
  J4 = screw terminal, 20 pins
  S2 = Round Pushbutton
  J5 = female pin header, 10 pins [form="♀ (female)"]
  J6 = female pin header, 8 pins [form="♀ (female)"]
  M1 = RioRand LM2596
  J11 = rounded female pin header, 1 pin [form="♀ (female rounded)"]
  J10 = rounded female pin header, 1 pin [form="♀ (female rounded)"]
  J8 = rounded female pin header, 1 pin [form="♀ (female rounded)"]
  J9 = rounded female pin header, 1 pin [form="♀ (female rounded)"]
  J12 = female pin header, 6 pins [form="♀ (female)"]  # not connected
  J7 = female pin header, 8 pins [form="♀ (female)"]

nets:
  N1: Componente3.D2, J4.pin14
  N2: Componente3.D3, J4.pin13
  N3: Componente3.D4, J4.pin12
  N4: Componente3.D5, J4.pin11
  N5: Componente3.D6, J4.pin10
  N6: Componente3.D7, J6.pin1
  N7: Componente3.D8, J5.pin10
  N8: Componente3.D9, J5.pin9
  N9: Componente3.D10, J4.pin9
  N10: Componente3.VIN, M1.Pin_3, J8.pin1
  GND: Componente3.GND, ZS-042_RTC1.GND, J4.pin7, J4.pin17, M1.Pin_4, J9.pin1, J7.pin6
  5V: Componente3.5V, ZS-042_RTC1.VCC, J4.pin8, J4.pin18, J7.pin5
  N11: Componente3.A7, J4.pin1
  N12: Componente3.A6, J4.pin2
  N13: Componente3.A5, ZS-042_RTC1.SCL, J4.pin16
  N14: Componente3.A4, ZS-042_RTC1.SDA, J4.pin15
  N15: Componente3.A3, J4.pin3
  N16: Componente3.A2, J4.pin4
  N17: Componente3.A1, J4.pin5
  N18: Componente3.A0, J4.pin6
  N19: J4.pin19, M1.Pin_2, J10.pin1
  N20: J4.pin20, S2.leg0
  N21: S2.leg1, M1.Pin_1, J11.pin1
